# Fritzing sketch BrewDooPrototype (saved by Fritzing 0.7.11b)
breadboards: 1

parts:
  Arduino1 = Arduino
  LCD1 = LCD screen
  R1 = Resistor [tolerance=±5% resistance=220 package=THT]
  R2 = Resistor [tolerance=±5% resistance=220 package=THT]
  R3 = Resistor [tolerance=±5% resistance=220 package=THT]
  R4 = Resistor [tolerance=±5% resistance=220 package=THT]
  R5 = Resistor [tolerance=±5% resistance=220 package=THT]
  R6 = Resistor [tolerance=±5% resistance=220 package=THT]
  LED1 = RGB LED (com. cathode, rgb) [package="5 mm [THT]"]
  LED2 = RGB LED (com. cathode, rgb) [package="5 mm [THT]"]
  S1 = Pushbutton [package="[THT]"]
  S2 = Pushbutton [package="[THT]"]

nets:
  N1: Arduino1.D13, LCD1.RS
  N2: Arduino1.D12, LCD1.E
  N3: Arduino1.D11, R4.Pin_0
  N4: Arduino1.D10, R5.Pin_0
  N5: Arduino1.D9, R6.Pin_0
  N6: Arduino1.D8, LCD1.DB4
  N7: Arduino1.D7, LCD1.DB5
  N8: Arduino1.D6, R1.Pin_0
  N9: Arduino1.D5, R2.Pin_0
  N10: Arduino1.D4, LCD1.DB6
  N11: Arduino1.D3, R3.Pin_0
  N12: Arduino1.D2, LCD1.DB7
  GND: Arduino1.D1TX, Arduino1.D0RX, Arduino1.GND, LCD1.VSS, LCD1.V0, LCD1.R/W, LCD1.LED-, LED1.common_cathode, LED2.common_cathode, S1.Pin_1, S1.Pin_2, S2.Pin_1, S2.Pin_2
  +5V: Arduino1.+5V, LCD1.VDD, LCD1.LED+
  N13: R1.Pin_1, LED1.blue_anode
  N14: R2.Pin_1, LED1.green_anode
  N15: R3.Pin_1, LED1.red_anode
  N16: R4.Pin_1, LED2.blue_anode
  N17: R5.Pin_1, LED2.green_anode
  N18: R6.Pin_1, LED2.red_anode
  N19: S1.Pin_3, S1.Pin_4
  N20: S2.Pin_3, S2.Pin_4
